# Fritzing sketch 1praktika (saved by Fritzing 0.9.3b)
breadboards: 1

parts:
  LED1 = LED - 5mm [color="Red (633nm)" package="5 mm [THT]"]
  R1 = Resistor [tolerance=±5% resistance=220 package=THT]
  R3 = Resistor [tolerance=±5% resistance=220 package=THT]  # not connected
  D1 = Rectifier Diode [part_number=1N4001 package="300 mil [THT]"]
  VCC1 = Battery

nets:
  N1: LED1.cathode, D1.anode
  N2: LED1.anode, R1.Pin_1
  N3: R1.Pin_0, VCC1.+
  N4: D1.cathode, VCC1.-

notes:
  R = 220 Ω
