# Fritzing sketch 2praktika (saved by Fritzing 0.9.3b)
breadboards: 1

parts:
  LED1 = LED - 5mm [color="Red (633nm)" package="5 mm [THT]"]
  R1 = Resistor [tolerance=±5% resistance=220 package=THT]
  R3 = Resistor [tolerance=±5% resistance=220 package=THT]  # not connected
  VCC1 = Battery
  U1 = SWITCH_SPDT [package=kps-1290]
  C1 = Capacitor Polarized [package=panasonic_d]

nets:
  N1: LED1.cathode, VCC1.-, C1.-
  N2: LED1.anode, R1.Pin_1
  N3: VCC1.+, U1.O

notes:
  R = 220 Ω
  Kondentsadorea C = 470 μF
