# Fritzing sketch 5praktika (saved by Fritzing 0.9.3b)
breadboards: 1

parts:
  Q1 = NPN-Transistor [package="SOT-23 [SMD]"]
  R1 = Resistor [tolerance=±5% resistance=220 package=THT]  # not connected
  R2 = Resistor [tolerance=±5% resistance=1.8k package=THT]  # not connected
  Q2 = NPN-Transistor [package="TO92 [THT]"]  # not connected
  LED1 = smd LED [color="Red (633nm)" package="0603 [SMD]"]
  R4 = Resistor [tolerance=±5% resistance=220 package=THT]
  R8 = Resistor [tolerance=±5% resistance=10k package=THT]  # not connected
  R9 = Resistor [tolerance=±5% resistance=1.8k package=THT]
  VCC1 = 4 x AAA Battery Mount
  R10 = Resistor [tolerance=±5% resistance=10k package=THT]
  R11 = Photocell (LDR) [package=THT]

nets:
  N1: Q1.2, VCC1.-, R11.pin_1
  N2: Q1.0, R9.Pin_0
  N3: Q1.1, LED1.cathode
  N4: LED1.anode, R4.Pin_0
  N5: R4.Pin_1, VCC1.+, R10.Pin_1
  N6: R9.Pin_1, R10.Pin_0, R11.pin_0

notes:
  R = 1,8kΩ
  R = 220Ω
  NPN BC 537 edo BC 538
  R = 10kΩ
