# Fritzing sketch 7praktika (saved by Fritzing 0.9.3b)
breadboards: 1

parts:
  Q1 = NPN-Transistor [package="SOT-23 [SMD]"]
  R1 = Resistor [tolerance=±5% resistance=220 package=THT]  # not connected
  R2 = Resistor [tolerance=±5% resistance=1k package=THT]  # not connected
  Q2 = NPN-Transistor [package="TO92 [THT]"]  # not connected
  LED1 = smd LED [color="Red (633nm)" package="0603 [SMD]"]
  R4 = Resistor [tolerance=±5% resistance=220 package=THT]
  R9 = Resistor [tolerance=±5% resistance=1k package=THT]
  R12 = Trimmer Potentiometer [maximum_resistance=10kΩ package=THT]
  VCC1 = 4 x AAA Battery Mount
  R13 = Trimmer Potentiometer [maximum_resistance=10kΩ package=THT]  # not connected
  R14 = Temperature Sensor (Thermistor) [thermistor_type=NTC package=THT]

nets:
  N1: Q1.2, R12.wiper, VCC1.-
  N2: Q1.0, R9.Pin_0
  N3: Q1.1, LED1.cathode
  N4: LED1.anode, R4.Pin_0
  N5: R4.Pin_1, VCC1.+, R14.pin_1
  N6: R9.Pin_1, R12.leg2, R14.pin_0

notes:
  R = 1kΩ
  R = 220Ω
  NPN BC 537 edo BC 538
  Rmax = 10kΩ
